// Logisim project Project.circ as structural Verilog: 3 circuits, main circuit main
module main (
);

  Adder adder_1 ();  // open: a1, b1, a2, b2, a3, b3, a4, b4, c1, out_10, c2, out_12, c3, out_14, c4, out_16
  Subtractor subtractor_1 ();  // open: a1, b1, a2, b2, a3, b3, a4, b4, out_9, out_10, out_11, out_12
endmodule

module Adder (
  input  [2:0] a1,
  input  [2:0] b1,
  input  [2:0] a2,
  input  [2:0] b2,
  input  [2:0] a3,
  input  [2:0] b3,
  input  [2:0] a4,
  input  [2:0] b4,
  output [2:0] c1,
  output out_10,
  output [2:0] c2,
  output out_12,
  output [2:0] c3,
  output out_14,
  output [2:0] c4,
  output out_16
);

  Adder_part #(.width(3)) adder_1 (.a(a1), .b(b1), .out(c1), .cout(out_10));  // open: cin
  Adder_part #(.width(3)) adder_2 (.a(a2), .b(b2), .out(c2), .cout(out_12));  // open: cin
  Adder_part #(.width(3)) adder_3 (.a(a3), .b(b3), .out(c3), .cout(out_14));  // open: cin
  Adder_part #(.width(3)) adder_4 (.a(a4), .b(b4), .out(c4), .cout(out_16));  // open: cin
endmodule

module Subtractor (
  input  [2:0] a1,
  input  [2:0] b1,
  input  [2:0] a2,
  input  [2:0] b2,
  input  [2:0] a3,
  input  [2:0] b3,
  input  [2:0] a4,
  input  [2:0] b4,
  output [2:0] out_9,
  output [2:0] out_10,
  output [2:0] out_11,
  output [2:0] out_12
);

  Subtractor_part #(.width(3)) subtractor_1 (.a(a1), .b(b1), .out(out_9));  // open: bin, bout
  Subtractor_part #(.width(3)) subtractor_2 (.a(a2), .b(b2), .out(out_10));  // open: bin, bout
  Subtractor_part #(.width(3)) subtractor_3 (.a(a3), .b(b3), .out(out_11));  // open: bin, bout
  Subtractor_part #(.width(3)) subtractor_4 (.a(a4), .b(b4), .out(out_12));  // open: bin, bout
endmodule
